# Fritzing sketch Project 1 Fritzing (saved by Fritzing 0.9.3b)
breadboards: 1

parts:
  Part1 = Arduino Uno (Rev3)  # not connected
  Part2 = 2A MOTOR SHIELD 9
  hc-sr1 = hc-sr04
  T1 = LM35 Temperature Sensor [package="TO92 [THT]"]
  J1 = Basic Servo
  M2 = DC Motor  # not connected
  M3 = DC Motor  # not connected

nets:
  N1: Part2.A1, J1.pulse
  N2: Part2.D13, hc-sr1.Trig
  N3: Part2.A0, T1.Vout
  N4: Part2.D12, hc-sr1.Echo
  VCC: hc-sr1.VCC, T1.+Vs, J1.vcc
  GND: hc-sr1.GND, T1.GND, J1.gnd
